# Fritzing sketch 0.ESP_Base (saved by Fritzing 0.9.3b)
breadboards: 1

parts:
  U1 = NodeMCU V3.0

nets:
  N1: U1.GND#6, U1.GND#13, U1.GND#16, U1.GND#33

notes:
  3V
  5V

custom parts:
  NodeMCU V3.0: ESP8266 based NodeMCU
