# Fritzing sketch 1.ESP_Led (saved by Fritzing 0.9.3b)
breadboards: 1

parts:
  U1 = NodeMCU V3.0
  LED2 = LED - 5mm [color="Red (633nm)" package="5 mm [THT]"]
  R3 = Resistor [tolerance=±5% resistance=220 package=THT]

nets:
  N1: U1.D0, R3.Pin_0
  N2: U1.GND#6, U1.GND#13, U1.GND#16, U1.GND#33, LED2.cathode
  N3: LED2.anode, R3.Pin_1

notes:
  3V
  5V

custom parts:
  NodeMCU V3.0: ESP8266 based NodeMCU
