# Fritzing sketch 2.ESP_DHT-LCD (saved by Fritzing 0.9.3b)
breadboards: 1

parts:
  Part1 = KY-015 Temperature & Humidity Sensor Module [package="Breakout board"]
  Componente1 = LCD1602-I2C
  U1 = NodeMCU V3.0

nets:
  N1: Part1.S, U1.D5
  VIN: Part1.Vin, Componente1.VCC, U1.VU
  N2: Part1.-, Componente1.GND, U1.GND#6, U1.GND#13, U1.GND#16, U1.GND#33
  N3: Componente1.SDA, U1.D3
  N4: Componente1.SCL, U1.D4

notes:
  3V

custom parts:
  KY-015 Temperature & Humidity Sensor Module: KY-015 temperature and humidity sensor module, provides a low-latency serial interface to measure humidity and temperature.
  LCD1602-I2C: A standard character display, usually with 2x16 characters. Comes in many colors with LCM1602 IIC attached.
  NodeMCU V3.0: ESP8266 based NodeMCU
