# Fritzing sketch 2.ESP_LCD (saved by Fritzing 0.9.3b)
breadboards: 1

parts:
  U1 = NodeMCU V3.0
  Componente2 = LCD1602-I2C

nets:
  N1: U1.D3, Componente2.SDA
  N2: U1.D4, Componente2.SCL
  N3: U1.GND#6, U1.GND#13, U1.GND#16, U1.GND#33, Componente2.GND
  VIN: U1.Vin, Componente2.VCC

notes:
  3V
  5V

custom parts:
  NodeMCU V3.0: ESP8266 based NodeMCU
  LCD1602-I2C: A standard character display, usually with 2x16 characters. Comes in many colors with LCM1602 IIC attached.
