# Fritzing sketch 4.ESP_DHT-LCD_rele (saved by Fritzing 0.9.3b)
breadboards: 1

parts:
  U1 = NodeMCU V3.0
  Componente2 = LCD1602-I2C
  Part2 = KY-015 Temperature & Humidity Sensor Module [package="Breakout board"]
  U2 = 2-Channel 5v Relay Shield [package=relay-2ch5v10a]

nets:
  N1: U1.D1, U2.IN2
  N2: U1.D2, Part2.S
  N3: U1.D3, Componente2.SDA
  N4: U1.D4, Componente2.SCL
  GND: U1.GND#6, U1.GND#13, U1.GND#16, U1.GND#33, Componente2.GND, Part2.-, U2.GND
  VIN: U1.Vin, Componente2.VCC, Part2.Vin, U2.VCC

notes:
  3V
  5V

custom parts:
  NodeMCU V3.0: ESP8266 based NodeMCU
  LCD1602-I2C: A standard character display, usually with 2x16 characters. Comes in many colors with LCM1602 IIC attached.
  KY-015 Temperature & Humidity Sensor Module: KY-015 temperature and humidity sensor module, provides a low-latency serial interface to measure humidity and temperature.
  2-Channel 5v Relay Shield: 2 Channel 5v Relay Shield w. 2x SPD-06VDC-SD-C
