# Fritzing sketch Led_pulsador (saved by Fritzing 0.9.3b)
breadboards: 1

parts:
  Componente1 = Arduino Uno (Rev3)
  R1 = Resistor [tolerance=±5% resistance=220 package=THT]
  LED1 = LED - 5mm [color="Red (633nm)" package="5 mm [THT]"]
  S1 = Momentary Switch [package=ksa_sealed_tac_switch]
  R2 = Resistor [tolerance=±5% resistance=220 package=THT]

nets:
  N1: Componente1.D11_PWM/MOSI, LED1.anode
  N2: Componente1.D2, S1.3, R2.Pin_1
  N3: Componente1.5V, S1.2
  N4: Componente1.GND, R1.Pin_1, R2.Pin_0
  N5: R1.Pin_0, LED1.cathode
