# Fritzing sketch MedidaHumedadSalinidad (saved by Fritzing 0.9.3b)
breadboards: 1

parts:
  Water_Level_Sensor1 = Water Level Sensor
  Componente1 = Arduino Uno (Rev3)

nets:
  N1: Water_Level_Sensor1.SIG, Componente1.A0
  VCC: Water_Level_Sensor1.VCC, Componente1.5V
  GND: Water_Level_Sensor1.GND, Componente1.GND

custom parts:
  Water Level Sensor: A water level sensor. This sensor operates at 3V to 5V. The Sig (signal) pin outputs an analogue signal that is in proportion to the amount of water in contact with the sensor.
