# Fritzing sketch SistemaRiegoRegulable (saved by Fritzing 0.9.3b)
breadboards: 1

parts:
  Water_Level_Sensor1 = Water Level Sensor
  Componente1 = Arduino Uno (Rev3)
  KY-1 = Keyes Relay [package=THT]
  R1 = Rotary Potentiometer (Small) [maximum_resistance=100kΩ package=THT]

nets:
  N1: Water_Level_Sensor1.SIG, Componente1.A0
  VCC: Water_Level_Sensor1.VCC, Componente1.5V, KY-1.power, R1.leg2
  GND: Water_Level_Sensor1.GND, Componente1.GND, KY-1.ground, R1.leg1
  N2: Componente1.A1, R1.wiper
  N3: Componente1.D8, KY-1.signal

custom parts:
  Water Level Sensor: A water level sensor. This sensor operates at 3V to 5V. The Sig (signal) pin outputs an analogue signal that is in proportion to the amount of water in contact with the sensor.
  Keyes Relay: The Keyes 5V relay module is suitable for SCM development, home appliance control. It uses a 5V~12V TIL control signal which can control DC / AC signal.
